# Fritzing sketch EngineRoomGuard (saved by Fritzing 0.9.9b)
circuit board: 7.6cm x 8.5cm

parts:
  U1 = ESP32-38PinWide [part_number=ESP32-38PinWide]
  LED1 = LED - 5mm [color="Red (633nm)" current=0.030 package="5 mm [THT]"]
  C1 = Electrolytic Capacitor [capacitance=0.47mF voltage=35V package="100 mil [THT, electrolytic]"]
  C2 = Electrolytic Capacitor [capacitance=0.47mF voltage=35V package="100 mil [THT, electrolytic]"]
  D1 = Schottky Diode [part_number=1N5817 package="300 mil [THT]"]
  R1 = Resistor [tolerance=±5% power=0.25 resistance=330 package=THT]
  U2_Alarm = RELAY-SIL05-1A72-71D [part_number=SIL05-1A package=relay-g5v]
  U3_Smoke = RELAY-SIL05-1A72-71D [part_number=SIL25-1A package=relay-g5v]
  U4_Eng_1_Oil = RELAY-SIL05-1A72-71D [part_number=SIL24-1A package=relay-g5v]
  U5_Eng_2_Oil = RELAY-SIL05-1A72-71D [part_number=SIL24-1A package=relay-g5v]
  R2 = Resistor [tolerance=±5% power=0.25 resistance=4.7k package=THT]
  J3_Int_Piezo = Screw terminal - 2 pins [package=THT]
  U6_Spare = RELAY-SIL05-1A72-71D [part_number=SIL24-1A package=relay-g5v]
  J1 = screw terminal, 14 pins
  J2 = screw terminal, 14 pins
  IC1 = Voltage Regulator [part_number=7805 package=to220-igo]

nets:
  N1: U1.GPIO32, U5_Eng_2_Oil.OUT
  N2: U1.GPIO33, U3_Smoke.OUT
  N3: U1.GPIO25, U4_Eng_1_Oil.OUT
  N4: U1.GPIO26, U6_Spare.OUT
  GND: U1.GND, LED1.cathode, C1.-, C2.-, U2_Alarm.COUT, U3_Smoke.IN, U4_Eng_1_Oil.IN, U5_Eng_2_Oil.IN, J3_Int_Piezo.pin2, U6_Spare.IN, J1.pin3, J1.pin13, J2.pin7, J2.pin9, J2.pin13, IC1.GND
  N5: U1.VIN, C2.+, R1.Pin_0, R2.Pin_0, J1.pin4, J2.pin14, IC1.OUT
  N6: U1.GPIO2, U1.GPIO4, U1.GPIO18, R2.Pin_1, J3_Int_Piezo.pin1, J1.pin2
  N7: U1.GPIO19, U2_Alarm.CIN
  N8: U1.GPIO21, J2.pin12
  N9: U1.GPIO22, J2.pin11
  N10: U1.GPIO23, J2.pin8
  N11: LED1.anode, R1.Pin_1
  N12: C1.+, D1.cathode, U2_Alarm.IN, IC1.IN
  N13: D1.anode, J1.pin14
  N14: U2_Alarm.OUT, J2.pin10
  N15: U3_Smoke.CIN, J1.pin12
  N16: U3_Smoke.COUT, J1.pin11
  N17: U4_Eng_1_Oil.CIN, J1.pin10
  N18: U4_Eng_1_Oil.COUT, J1.pin9
  N19: U5_Eng_2_Oil.CIN, J1.pin8
  N20: U5_Eng_2_Oil.COUT, J1.pin7
  N21: U6_Spare.CIN, J1.pin6
  N22: U6_Spare.COUT, J1.pin5

notes:
  R1
  5V Power LED
  Int Buzzer
  U4 Eng 1 Oil
  U5 Eng 2 Oil
  U2 Alarm
  U3 Smoke
  U6 Spare
  Input pin 1
  R2
  Input pin 14
  Output pin 1
  Output pin 14
  EngineRoomGuard v2 2022

custom parts:
  ESP32-38PinWide: Generic 38-Pin ESP32 with wide format (only access to one side of pins on a breadboard) based on Stephen Lilley's HiLetgo ESP-WROOM-32 ESP32 ESP-32S Development Board.
  RELAY-SIL05-1A72-71D: MEDER SIL05-1A72-71D RSコンポーネンツ 349-2884
